# Fritzing sketch sketch (saved by Fritzing 0.9.3b)
circuit board: 5.89596cm x 6.96652cm
breadboards: 2

parts:
  Nokia_5110_LCD_Module1 = Nokia 5110 LCD basado en PCD8544
  Joystick = Thumb Joystick
  Arduino_Micro = Arduino Micro (Rev3)
  R1 = Resistor [tolerance=±5% resistance=330 package="1206 [SMD]"]
  R2 = Resistor [tolerance=±5% resistance=10k package="1206 [SMD]"]
  R3 = Resistor [tolerance=±5% resistance=10k package="1206 [SMD]"]
  R4 = Resistor [tolerance=±5% resistance=10k package="1206 [SMD]"]
  R5 = Resistor [tolerance=±5% resistance=1k package="1206 [SMD]"]
  R6 = Resistor [tolerance=±5% resistance=10k package="1206 [SMD]"]

nets:
  VCC: Nokia_5110_LCD_Module1.VCC, Arduino_Micro.3V3
  GND: Nokia_5110_LCD_Module1.GND, Arduino_Micro.GND
  N1: Nokia_5110_LCD_Module1.CE, R5.Pin_1
  N2: Nokia_5110_LCD_Module1.RST, R6.Pin_1
  N3: Nokia_5110_LCD_Module1.DC, R4.Pin_1
  N4: Nokia_5110_LCD_Module1.DIN, R3.Pin_1
  N5: Nokia_5110_LCD_Module1.CLK, R2.Pin_1
  N6: Nokia_5110_LCD_Module1.LIGHT, R1.Pin_1
  N7: Joystick.SEL, Arduino_Micro.D3/SCL
  N8: Joystick.HORZ, Arduino_Micro.A0
  N9: Joystick.VERT, Arduino_Micro.A1
  N10: Joystick.VCC, Arduino_Micro.RESET
  N11: Arduino_Micro.MOSI, R3.Pin_0
  N12: Arduino_Micro.D2/SDA, R1.Pin_0
  N13: Arduino_Micro.D5_PWM, R4.Pin_0
  N14: Arduino_Micro.D6_PWM/A7, R6.Pin_0
  N15: Arduino_Micro.D7, R5.Pin_0
  N16: Arduino_Micro.SCK, R2.Pin_0

custom parts:
  Nokia 5110 LCD basado en PCD8544: Módulo Nokia 5110 LCD basado en el controlador PCD8544. Versión de 8 pines (sólo entrada).
